# Fritzing sketch Sketch (saved by Fritzing 0.9.3b)
breadboards: 1

parts:
  Componente1 = Arduino Mega ADK (Rev3)  # not connected
  Componente2 = Arduino Ethernet Shield (Rev3)  # not connected
  Componente3 = Barometric Pressure Sensor - BMP085 Breakout  # not connected
  RHT1 = Humidity and Temperature Sensor RHT03  # not connected
  Componente4 = Gas Sensor Breakout Board  # not connected
  R1 = Resistor [tolerance=±5% resistance=220 package=THT]
  R2 = Resistor [tolerance=±5% resistance=220 package=THT]
  R3 = Resistor [tolerance=±5% resistance=220 package=THT]
  R4 = Resistor [tolerance=±5% resistance=220 package=THT]
  R5 = Resistor [tolerance=±5% resistance=220 package=THT]
  R6 = Resistor [tolerance=±5% resistance=220 package=THT]
  Componente5 = Real Time Clock Module - DS1307 RTC Breakout Board  # not connected
  R7 = Resistor [tolerance=±5% resistance=220 package=THT]
  R8 = Resistor [tolerance=±5% resistance=220 package=THT]
  R9 = Resistor [tolerance=±5% resistance=220 package=THT]  # not connected
  Q1 = NPN-Transistor [package="TO92 [THT]"]  # not connected
  Q2 = NPN-Transistor [package="TO92 [THT]"]  # not connected
  LED1 = LED - 5mm [color="Yellow (595nm)" package="5 mm [THT]"]  # not connected
  LED2 = LED - 5mm [color="Red (633nm)" package="5 mm [THT]"]  # not connected

nets:
  N1: R1.Pin_0, R2.Pin_0
  N2: R1.Pin_1, R2.Pin_1
  N3: R3.Pin_0, R4.Pin_0
  N4: R3.Pin_1, R4.Pin_1
  N5: R5.Pin_0, R6.Pin_0
  N6: R5.Pin_1, R6.Pin_1
  N7: R7.Pin_0, R8.Pin_0
  N8: R7.Pin_1, R8.Pin_1
